# Fritzing sketch CircuitDiagram (saved by Fritzing 0.9.0b)
breadboards: 1

parts:
  U1 = Spark Core (v1.0)
  U3 = LCD-16X2 [package=lcd-16x2_nosilk]

nets:
  N1: U1.A2, U1.3V3
  N2: U1.A3, U1.A6
  N3: U1.A5, U1.VIN
  GND: U1.GND, U3.VSS
  N4: U1.D0, U3.RS
  N5: U1.D1, U3.R_W
  N6: U1.D2, U3.E
  N7: U1.D3, U3.DB4
  N8: U1.D4, U3.DB5
  N9: U1.D5, U3.DB6
  N10: U1.D6, U3.DB7
  N11: U1.3V3*, U3.VDD

custom parts:
  Spark Core (v1.0): The Spark Core is a tiny Wi-Fi development board that makes it easy to create internet-connected hardware. The Core is all you need to get started; power it over USB and in minutes you'll be controlling LEDs, switches and motors and collecting data from sensors over the internet! It has 8 digital I/O pins, 8 analog I/O pins, 8 PWM pins; UART (Serial), SPI, I2C, and JTAG peripherals available.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
